# Fritzing sketch GarageRemoteSchematics (saved by Fritzing 0.9.3b)
breadboards: 1
perfboards: 1

parts:
  Part1 = Arduino Uno (Rev3)
  Part2 = Bluetooth HC-05 Macho
  U1 = RELAY [package=OJ]
  D1 = Diode [package=diode-1n4148]  # not connected

nets (from the breadboard view):
  N1: Part1.D10_PWM/SS, U1.COIL1
  N2: Part1.D0/RX, Part2.TXD
  N3: Part1.D1/TX, Part2.RXD
  5V: Part1.5V, Part2.VCC
  GND: Part1.GND, Part2.GND, U1.COIL2

notes:
  Garage Door wire trigger
